// Logisim project aufgabe9_3.circ as structural Verilog: 2 circuits, main circuit main
module main (
  input  in_1,
  input  in_2
);

  wire pull_resistor_1_node;

  Pull_Resistor #(.pull(1)) pull_resistor_1 (.node(pull_resistor_1_node));
  Transistor #(.\type ("n")) transistor_1 (.in(1'b0), .out(pull_resistor_1_node), .gate(in_1));
  Transistor #(.\type ("n")) transistor_2 (.in(1'b0), .out(pull_resistor_1_node), .gate(in_2));
endmodule

module tristate (
  input  in_1,
  input  in_2
);

  wire controlled_buffer_1_out;

  assign controlled_buffer_1_out = 1'b1 ? in_1 : 1'bz;  // Controlled_Buffer controlled_buffer_1
  LED led_1 (.in(controlled_buffer_1_out));
  assign controlled_buffer_1_out = 1'b1 ? in_2 : 1'bz;  // Controlled_Buffer controlled_buffer_2
endmodule
